# Fritzing sketch Farmlynk main (saved by Fritzing 0.9.4)
breadboards: 1

parts:
  YwRobot_Power_Supply1 = YwRobot Breadboard Power Supply [part_number=545043]
  U2 = NodeMCU V1.0
  KY-1 = Keyes Relay [package=THT]
  KY-2 = Keyes Relay [package=THT]
  Part1 = Soil Moisture Sensor
  Part2 = Soil Moisture Sensor
  U3 = Vibration Motor- ROB-08449 [package=vibe-motor-10mm]
  U4 = Vibration Motor- ROB-08449 [package=vibe-motor-10mm]
  HC-SR04_Sensor_1 = HC-SR04 Ultrasonic Distance Sensor
  Part3 = Arduino Uno (Rev3) - ICSP
  KY-3 = Keyes Relay [package=THT]

nets:
  N1: YwRobot_Power_Supply1.VCC#5, YwRobot_Power_Supply1.VCC#6, KY-1.power, KY-2.power
  N2: YwRobot_Power_Supply1.VCC#9, YwRobot_Power_Supply1.VCC#10, KY-1.C, KY-2.C, HC-SR04_Sensor_1.VCC, KY-3.power
  N3: YwRobot_Power_Supply1.GND#11, YwRobot_Power_Supply1.GND#12, KY-1.ground, KY-2.ground
  N4: YwRobot_Power_Supply1.GND#13, YwRobot_Power_Supply1.GND#14, U3.+, U4.+, HC-SR04_Sensor_1.GND, KY-3.ground
  N5: U2.D1, HC-SR04_Sensor_1.TRIG
  N6: U2.D2, HC-SR04_Sensor_1.ECHO
  3V3: U2.3V3, Part2.VCC
  GND: U2.GND, Part2.GND
  N7: U2.D5, KY-1.signal
  N8: U2.D6, KY-2.signal
  N9: U2.A0, Part2.SIG
  N10: KY-1.NC, U3.-
  N11: KY-2.NC, U4.-
  VCC: Part1.VCC, Part3.5V
  N12: Part3.D6_PWM, KY-3.signal

custom parts:
  YwRobot Breadboard Power Supply: The YwRobot Breadboard Power Supply (MB-V2) has two power rails; they can be 5V or 3V3. Power to the module can be provided through the female USB socket or through the A10 (female) 2.1mm power jack.
  NodeMCU V1.0: ESP8266 based NodeMCU
  Keyes Relay: The Keyes 5V relay module is suitable for SCM development, home appliance control. It uses a 5V~12V TIL control signal which can control DC / AC signal.
